# Fritzing sketch esquema_do_circuito-Braço_Robótico (saved by Fritzing 0.8.7b)
breadboards: 2

parts:
  S1 = Pushbutton [package="[THT]"]
  S2 = Pushbutton [package="[THT]"]
  S3 = Pushbutton [package="[THT]"]
  S4 = Pushbutton [package="[THT]"]
  S5 = Pushbutton [package="[THT]"]
  S6 = Pushbutton [package="[THT]"]
  S7 = Pushbutton [package="[THT]"]
  Componente1 = Arduino Uno (Rev3)
  R1 = Resistor [tolerance=±5% resistance=10k package=THT]
  R2 = Resistor [tolerance=±5% resistance=10k package=THT]
  R3 = Resistor [tolerance=±5% resistance=10k package=THT]
  R4 = Resistor [tolerance=±5% resistance=10k package=THT]
  R5 = Resistor [tolerance=±5% resistance=10k package=THT]
  R6 = Resistor [tolerance=±5% resistance=10k package=THT]
  R7 = Resistor [tolerance=±5% resistance=10k package=THT]
  J1 = Basic Servo
  J2 = Basic Servo
  J3 = Basic Servo
  J4 = Basic Servo

nets:
  N1: S1.Pin_1, S1.Pin_2
  N2: S1.Pin_3, S1.Pin_4, Componente1.D2, R3.Pin_0
  N3: S2.Pin_1, S2.Pin_2
  N4: S2.Pin_3, S2.Pin_4, Componente1.D4, R1.Pin_0
  N5: S3.Pin_1, S3.Pin_2
  N6: S3.Pin_3, S3.Pin_4, Componente1.D7, R7.Pin_0
  N7: S4.Pin_1, S4.Pin_2
  N8: S4.Pin_3, S4.Pin_4, Componente1.D10_PWM/SS, R6.Pin_0
  N9: S5.Pin_1, S5.Pin_2
  N10: S5.Pin_3, S5.Pin_4, Componente1.D3_PWM, R2.Pin_0
  N11: S6.Pin_1, S6.Pin_2
  N12: S6.Pin_3, S6.Pin_4, Componente1.D12/MISO, R5.Pin_0
  N13: S7.Pin_1, S7.Pin_2
  N14: S7.Pin_3, S7.Pin_4, Componente1.D13/SCK, R4.Pin_0
  N15: Componente1.D9_PWM, J3.pulse
  N16: Componente1.D11_PWM/MOSI, J4.pulse
  N17: Componente1.D5_PWM, J1.pulse
  N18: Componente1.D6_PWM, J2.pulse
  VCC: Componente1.5V, J1.vcc, J2.vcc, J3.vcc, J4.vcc
  GND: Componente1.GND, R1.Pin_1, R2.Pin_1, R3.Pin_1, R4.Pin_1, R5.Pin_1, R6.Pin_1, R7.Pin_1, J1.gnd, J2.gnd, J3.gnd, J4.gnd
